# Fritzing sketch client-with-sensor (saved by Fritzing 0.9.3b)

parts:
  U2 = ESP32-38PinWide [part_number=ESP32-38PinWide]
  HC-SR04_Sensor_1 = HC-SR04 Ultrasonic Distance Sensor
  220V_AC_to_5V_DC = HLK-PM01
  Source = AC Power [voltage=220 frequency=60]

nets:
  N1: U2.GPIO25, HC-SR04_Sensor_1.GND
  N2: U2.GPIO26, HC-SR04_Sensor_1.TRIG
  VIN: U2.VIN, HC-SR04_Sensor_1.VCC, 220V_AC_to_5V_DC.+Vo
  N3: U2.GND, HC-SR04_Sensor_1.ECHO, 220V_AC_to_5V_DC.-Vo
  N4: 220V_AC_to_5V_DC.AC#0, Source.V+
  N5: 220V_AC_to_5V_DC.AC#1, Source.V-

custom parts:
  ESP32-38PinWide: Generic 38-Pin ESP32 with wide format (only access to one side of pins on a breadboard) based on Stephen Lilley's HiLetgo ESP-WROOM-32 ESP32 ESP-32S Development Board.
