# Fritzing sketch server-with-relay (saved by Fritzing 0.9.3b)

parts:
  U1 = ESP32-38PinWide [part_number=ESP32-38PinWide]
  Op-Mode = Toggle Switch [package=THT]
  Manual-On/Off = Toggle Switch [package=THT]
  Relay = RELAY [package=relay-g5q]
  Pump = DC Motor
  220v_AC_to_5v_DC = HLK-PM01
  220V1 = AC Power [voltage=220 frequency=60]
  Status-Screeen = Grove OLED 128x96
  Buzzer = Buzzer 12mm [package=buzzer-ccv-kit]

nets:
  N1: U1.3.3, Manual-On/Off.L2, 220v_AC_to_5v_DC.+Vo, Status-Screeen.VCC
  N2: U1.GPIO25, Op-Mode.L2
  N3: U1.GPIO27, Buzzer.2
  GND: U1.GND, Relay.COIL1, 220v_AC_to_5v_DC.-Vo, Status-Screeen.GND, Buzzer.1
  N4: U1.GPIO21, Status-Screeen.SCL
  N5: U1.GPIO22, Status-Screeen.SDA
  N6: Op-Mode.L1, Manual-On/Off.COM
  N7: Op-Mode.COM, Relay.COIL2
  N8: Relay.MAIN, 220v_AC_to_5v_DC.AC#1, 220V1.V-
  N9: Relay.NO, Pump.pin_1
  N10: Pump.pin_2, 220v_AC_to_5v_DC.AC#0, 220V1.V+

custom parts:
  ESP32-38PinWide: Generic 38-Pin ESP32 with wide format (only access to one side of pins on a breadboard) based on Stephen Lilley's HiLetgo ESP-WROOM-32 ESP32 ESP-32S Development Board.
